# Fritzing sketch aplique (saved by Fritzing 0.9.3b)
circuit board: 3.56969cm x 7.37443cm
breadboards: 1

parts:
  JACK1 = 2.1mm Barrel Jack with Terminal Block
  R1 = Resistor [tolerance=±5% resistance=220 package=THT]
  J2 = male pin header, 8 pins [form="♂ (male)"]
  J3 = male pin header, 8 pins [form="♂ (male)"]
  J1 = male pin header, 3 pins [form="♂ (male)"]
  R2 = Resistor [tolerance=±5% resistance=220 package=THT]
  WeMos_D1_Mini2 = WeMos D1 Mini  # not connected
  J4 = male pin header, 2 pins [form="♂ (male)"]
  J5 = male pin header, 2 pins [form="♂ (male)"]
  NEOPIXEL1 = Neopixel Strip -- White (60/m)  # not connected

nets:
  N1: JACK1.POS, J3.pin1, J1.pin3, J4.pin2, J5.pin2
  N2: JACK1.NEG, R1.Pin_1, J3.pin2, J1.pin1, R2.Pin_1
  N3: R1.Pin_0, J2.pin5, J4.pin1
  N4: J2.pin4, J1.pin2
  N5: J2.pin6, R2.Pin_0, J5.pin1

custom parts:
  Neopixel Strip -- White (60/m): Neopixel Strip, White, 60 pixels per meter.
